# Fritzing sketch Spark-Lamp (saved by Fritzing 0.9.1b)
breadboards: 1

parts:
  Part1 = Spark Core (v1.0)
  U1 = RF-LINK_TX [package=rf-link_tx]
  ANT2 = Antenna
  S3 = Pushbutton [package=THT]
  S4 = Pushbutton [package=THT]
  R2 = Photocell (LDR) [package=THT]
  LED2 = LED - 5mm [color="Red (633nm)" package="5 mm [THT]"]
  U3 = OPA344 [package=sot23-5]
  R3 = Resistor [tolerance=±5% resistance=10k package=THT]
  R4 = Resistor [tolerance=±5% resistance=10k package=THT]
  R5 = Resistor [tolerance=±5% resistance=10k package=THT]
  R6 = Resistor [tolerance=±5% resistance=10k package=THT]
  U4 = DIODE-ZENER [package=diode-zener]

nets:
  N1: Part1.A7, R6.Pin_1, U4.C
  GND: Part1.GND, U1.GND, S3.leg0, S4.leg0, R2.pin_0, LED2.cathode, U3.V-, R5.Pin_0, U4.A
  5V: Part1.VIN, U1.+5V, U3.V+, R3.Pin_1, R4.Pin_1
  N2: Part1.D0, U1.DATA
  N3: Part1.D2, S3.leg1
  N4: Part1.D4, S4.leg1
  N5: U1.ANT, ANT2.antenna_lead
  N6: R2.pin_1, U3.-IN, R3.Pin_0
  120V: LED2.anode
  N7: U3.OUT, R6.Pin_0
  N8: U3.+IN, R4.Pin_0, R5.Pin_1
